# Fritzing sketch fritzing_diagram (saved by Fritzing 0.9.4)
breadboards: 1

parts:
  Part12 = Arduino Mega 2560 (Rev3)
  Keypad4x2 = Membran Keypad 4x4
  Part13 = Gravity Analog Sound Level Meter
  8x32_-_256_LED_Addressable_Matrix1 = 8x32 - 256 LED Addressable Matrix  # not connected
  8x32_-_256_LED_Addressable_Matrix2 = 8x32 - 256 LED Addressable Matrix  # not connected
  U2 = LED Matrix 8x32
  LCD2004-I2C1 = LCD2004-I2C
  JACK2 = 2.1mm Barrel Jack with Terminal Block
  C8 = Electrolytic Capacitor [capacitance=1000µF package="300 mil [THT, electrolytic]"]
  R1 = Resistor [tolerance=±5% resistance=220 package=THT]

nets:
  N1: Part12.A1, Part13.A
  N2: Part12.D21/SCL, LCD2004-I2C1.SCL
  N3: Part12.D20/SDA, LCD2004-I2C1.SDA
  GND: Part12.GND, Part13.GND, U2.GND, LCD2004-I2C1.GND, JACK2.NEG, C8.-
  N4: Part12.D12_PWM, R1.Pin_1
  5V: Part12.5V, Part13.5V, U2.VCC, LCD2004-I2C1.VCC, JACK2.POS, C8.+
  N5: Part12.D23, Keypad4x2.Pin1
  N6: Part12.D25, Keypad4x2.Pin2
  N7: Part12.D27, Keypad4x2.Pin3
  N8: Part12.D29, Keypad4x2.Pin4
  N9: Part12.D31, Keypad4x2.Pin5
  N10: Part12.D33, Keypad4x2.Pin6
  N11: Part12.D35, Keypad4x2.Pin7
  N12: Part12.D37, Keypad4x2.Pin8
  N13: U2.OUT, R1.Pin_0

custom parts:
  Membran Keypad 4x4: Membrane Keypad 4x4 Matrix
  Gravity Analog Sound Level Meter: In our environment, there are all kinds of sounds, some of which are quite noisy. With the development of human civilization, the quiet environments have become few and far between, and are replaced with more and more noisy environments instead. Staying in the loud places for long time will have an impact on hearing, which is bad for health. Sound level meter (also known as the decibel meter,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
  8x32 - 256 LED Addressable Matrix: 1. : pixel RGB , IC WS2812 2. Work voltage: DC 5V 3. Power: 0.3W/pixel 6. waterproof level: Non-waterproof 7. Working mode: external controller Arduino compatible. 8. Connection: VCC: RED; GND:BLACK; DAT:BLUE
  LED Matrix 8x32: It's an LED Matrix with 256 individually addressable LEDs. That's it.
  LCD2004-I2C: A standard character display with 4x20 characters. Comes in many colors with LCM2004 IIC attached.
